// Logisim project Computer.circ as structural Verilog: 13 circuits, main circuit Main
module Main (
);

  wire and_1_out, and_2_out, clock_1_out, controlled_buffer_1_out, controlled_buffer_11_out,
       DataType_Decoder_iq1a_d, DataType_Decoder_iq1out, DataType_Decoder_iq2a_d, DataType_Decoder_iq2out,
       decoder_1_out0, IQ_Controller_stop, memunit_1_clockout, memunit_1_ld, not_1_out, not_2_out, not_3_out,
       not_4_out, or_1_out, or_2_out, Reset_out;
  wire [1:0] extraregistercontroller_1_er0_we_oe, extraregistercontroller_1_er1_we_oe,
       extraregistercontroller_1_er2_we_oe, extraregistercontroller_1_er3_we_oe,
       extraregistercontroller_1_er4_we_oe, extraregistercontroller_1_er5_we_oe,
       extraregistercontroller_1_er6_we_oe, extraregistercontroller_1_er7_we_oe, QC_queuesize,
       typedecoderunit_1_out_3;
  wire [2:0] Instr_Type_Decoder_alu, Instr_Type_Decoder_cj, Instr_Type_Decoder_erc, Instr_Type_Decoder_rc1,
       Instr_Type_Decoder_rc2;
  wire [3:0] IQ_Controller_state, typedecoderunit_1_out_2;
  wire [4:0] alu_1_flagout, and_3_out, decoder_1_out1, Flag_q;
  wire [15:0] Address_Bus, alu_1_divremainder, alu_1_output, Data_Bus, DivOut_q, Instruction_q, IQ1Addr_out,
       IQ1Data_out, IQ2Addr_out, IQ2Data_out, memunit_1_address, portunit_1_porta_out, Program_Counter_q,
       Queue_1_q, Queue_2_q, ram_1_data, RegA_q, RegB_q, register_1_q, register_2_q;
  wire [31:0] CS1;

  CentralUnit centralunit_1 (.ControlSignal_0_31(CS1), .Instruction(Instruction_q[5:0]), .OE(and_2_out));
  not not_1 (not_1_out, and_1_out);
  assign controlled_buffer_1_out = and_1_out ? not_1_out : 1'bz;  // Controlled_Buffer controlled_buffer_1
  RAM #(.addrWidth(16), .dataWidth(16), .Select("low")) ram_1 (
    .addr(memunit_1_address), .data(ram_1_data), .clk(memunit_1_clockout), .ld(memunit_1_ld));  // open: sel, clr
  Register #(.width(16), .trigger("falling"), .Select("low")) Instruction (
    .D(Data_Bus), .en(IQ_Controller_state[0]), .Q(Instruction_q), .clk(clock_1_out), .clr(Reset_out));
  Register #(.width(16), .trigger("falling"), .Select("low")) Queue_1 (
    .D(Data_Bus), .en(IQ_Controller_state[1]), .Q(Queue_1_q), .clk(clock_1_out), .clr(Reset_out));
  Register #(.width(16), .trigger("falling"), .Select("low")) Queue_2 (
    .D(Data_Bus), .en(IQ_Controller_state[2]), .Q(Queue_2_q), .clk(clock_1_out), .clr(Reset_out));
  TypeDecoderUnit typedecoderunit_1 (
    .Instruction(Instruction_q[5:0]), .out_2(typedecoderunit_1_out_2), .out_3(typedecoderunit_1_out_3));
  assign Data_Bus = CS1[18] ? Program_Counter_q : 16'bz;  // Controlled_Buffer controlled_buffer_2
  Counter #(.width(16), .max('hffff), .trigger("falling"), .behavior("old")) Program_Counter (
    .load(and_1_out), .D(Data_Bus), .count(controlled_buffer_1_out), .Q(Program_Counter_q),
    .clk(clock_1_out), .clr(Reset_out));  // open: carry, preset
  and and_1 (and_1_out, CS1[17], controlled_buffer_11_out);
  MemUnit memunit_1 (
    .ADDRIN(controlled_buffer_1_out), .DataBusOut(Data_Bus), .DataBusIn(Data_Bus), .WE(CS1[14]),
    .OE(or_1_out), .AddressBus(Address_Bus), .Clock(clock_1_out), .Address(memunit_1_address),
    .ClockOut(memunit_1_clockout), .ld(memunit_1_ld), .DataIn(ram_1_data), .DataOut(ram_1_data));
  or or_1 (or_1_out, controlled_buffer_1_out, CS1[13]);
  assign Address_Bus = controlled_buffer_1_out ? Program_Counter_q : 16'bz;  // Controlled_Buffer controlled_buffer_3
  not Stop (controlled_buffer_1_out, IQ_Controller_stop);
  InstructionQueueController IQ_Controller (
    .Clock(clock_1_out), .Reset(Reset_out), .State(IQ_Controller_state), .Stop(IQ_Controller_stop),
    .QueueSize(QC_queuesize));  // open: Prevision
  QueueSizeDecoder QC (.DataType(typedecoderunit_1_out_3), .QueueSize(QC_queuesize));
  and and_2 (and_2_out, IQ_Controller_stop, clock_1_out);
  assign IQ1Addr_out = not_2_out ? Queue_1_q : 16'bz;  // Controlled_Buffer IQ1Addr
  not not_2 (not_2_out, DataType_Decoder_iq1a_d);
  assign IQ1Data_out = DataType_Decoder_iq1a_d ? Queue_1_q : 16'bz;  // Controlled_Buffer IQ1Data
  assign IQ2Addr_out = not_3_out ? Queue_2_q : 16'bz;  // Controlled_Buffer IQ2Addr
  not not_3 (not_3_out, DataType_Decoder_iq2a_d);
  assign IQ2Data_out = DataType_Decoder_iq2a_d ? Queue_2_q : 16'bz;  // Controlled_Buffer IQ2Data
  DataTypeDecoder DataType_Decoder (
    .DataType(typedecoderunit_1_out_3), .IQ1A_D(DataType_Decoder_iq1a_d), .IQ2A_D(DataType_Decoder_iq2a_d),
    .IQ1Out(DataType_Decoder_iq1out), .IQ2Out(DataType_Decoder_iq2out), .Stop(and_2_out));
  InstructionTypeDecoder Instr_Type_Decoder (
    .Arg1(Instruction_q[8:6]), .Arg2(Instruction_q[11:9]), .InstructionType(typedecoderunit_1_out_2),
    .RC1(Instr_Type_Decoder_rc1), .RC2(Instr_Type_Decoder_rc2), .ALU(Instr_Type_Decoder_alu),
    .CJ(Instr_Type_Decoder_cj), .ERC(Instr_Type_Decoder_erc));
  assign Address_Bus = DataType_Decoder_iq1out ? IQ1Addr_out : 16'bz;  // Controlled_Buffer controlled_buffer_4
  assign Data_Bus = DataType_Decoder_iq1out ? IQ1Data_out : 16'bz;  // Controlled_Buffer controlled_buffer_5
  assign Address_Bus = DataType_Decoder_iq2out ? IQ2Addr_out : 16'bz;  // Controlled_Buffer controlled_buffer_6
  assign Data_Bus = DataType_Decoder_iq2out ? IQ2Data_out : 16'bz;  // Controlled_Buffer controlled_buffer_7
  Clock clock_1 (.out(clock_1_out));
  Button Reset (.out(Reset_out));
  Pull_Resistor pull_resistor_1 (.node(Instr_Type_Decoder_alu));
  assign Data_Bus = CS1[11] ? alu_1_output : 16'bz;  // Controlled_Buffer controlled_buffer_8
  ExtraRegisterController extraregistercontroller_1 (
    .ERC(Instr_Type_Decoder_erc), .WE(CS1[15]), .OE(CS1[16]),
    .ER0_WE_OE(extraregistercontroller_1_er0_we_oe), .ER1_WE_OE(extraregistercontroller_1_er1_we_oe),
    .ER2_WE_OE(extraregistercontroller_1_er2_we_oe), .ER3_WE_OE(extraregistercontroller_1_er3_we_oe),
    .ER4_WE_OE(extraregistercontroller_1_er4_we_oe), .ER5_WE_OE(extraregistercontroller_1_er5_we_oe),
    .ER6_WE_OE(extraregistercontroller_1_er6_we_oe), .ER7_WE_OE(extraregistercontroller_1_er7_we_oe));
  Register #(.width(16), .trigger("falling"), .Select("low")) RegA (
    .D(Data_Bus), .en(extraregistercontroller_1_er0_we_oe[0]), .Q(RegA_q), .clk(clock_1_out), .clr(Reset_out));
  assign Data_Bus = extraregistercontroller_1_er2_we_oe[1] ? register_1_q : 16'bz;  // Controlled_Buffer controlled_buffer_9
  RegisterUnit Register_Unit (
    .ControlSignal_1(Instr_Type_Decoder_rc1), .ControlSignal_2(Instr_Type_Decoder_rc2), .Clock(clock_1_out),
    .OE_WE_2(CS1[7]), .RE_1(CS1[4]), .RE_2(CS1[5]), .OE_WE_1(CS1[6]), .Data_Bus(Data_Bus),
    .ADDR_DATA_1(CS1[8]), .ADDR_DATA_2(CS1[9]), .DataBus_Out(Data_Bus), .AddressBus_Out(Address_Bus),
    .Reset(Reset_out));
  assign Data_Bus = extraregistercontroller_1_er4_we_oe[1] ? DivOut_q : 16'bz;  // Controlled_Buffer controlled_buffer_10
  ALU alu_1 (
    .CalcOption(Instr_Type_Decoder_alu), .DivRemainder(alu_1_divremainder), .PortA(RegA_q), .PortB(RegB_q),
    .Output(alu_1_output), .FlagOut(alu_1_flagout));
  Register #(.width(16), .trigger("falling"), .Select("low")) RegB (
    .D(Data_Bus), .en(extraregistercontroller_1_er1_we_oe[0]), .Q(RegB_q), .clk(clock_1_out), .clr(Reset_out));
  Register #(.width(16), .Select("low")) register_1 (
    .D(Data_Bus), .en(extraregistercontroller_1_er2_we_oe[0]), .Q(register_1_q), .clk(clock_1_out),
    .clr(Reset_out));
  assign controlled_buffer_11_out = decoder_1_out0 ? decoder_1_out0 : 1'bz;  // Controlled_Buffer controlled_buffer_11
  Register #(.width(16), .trigger("falling"), .Select("low")) DivOut (
    .D(alu_1_divremainder), .en(CS1[12]), .Q(DivOut_q), .clk(clock_1_out), .clr(Reset_out));
  Register #(.width(5), .trigger("falling"), .Select("low")) Flag (
    .D(alu_1_flagout), .en(CS1[12]), .Q(Flag_q), .clk(clock_1_out), .clr(Reset_out));
  Decoder #(.select(3), .enable("false")) decoder_1 (
    .out0(decoder_1_out0), .out1(decoder_1_out1[0]), .out2(decoder_1_out1[1]), .out3(decoder_1_out1[2]),
    .out4(decoder_1_out1[3]), .out5(decoder_1_out1[4]), .sel(Instr_Type_Decoder_cj));  // open: out6, out7
  Register #(.width(16), .trigger("falling"), .Select("low")) register_2 (
    .D(Data_Bus), .en(extraregistercontroller_1_er3_we_oe[0]), .Q(register_2_q), .clk(clock_1_out),
    .clr(Reset_out));
  assign Data_Bus = extraregistercontroller_1_er3_we_oe[1] ? register_2_q : 16'bz;  // Controlled_Buffer controlled_buffer_12
  assign controlled_buffer_11_out = not_4_out ? or_2_out : 1'bz;  // Controlled_Buffer controlled_buffer_13
  not not_4 (not_4_out, decoder_1_out0);
  Pull_Resistor pull_resistor_2 (.node(decoder_1_out0));
  assign and_3_out = Flag_q & decoder_1_out1;  // AND_Gate and_3, 5 bits wide
  Pull_Resistor pull_resistor_3 (.node(decoder_1_out1));
  PortUnit portunit_1 (
    .PORTADDRWE(extraregistercontroller_1_er5_we_oe[0]), .PortA_In(portunit_1_porta_out), .PORTWE(CS1[19]),
    .PORTOE(CS1[20]), .DataBusOut(Data_Bus), .DataBusIn(Data_Bus), .PortA_Out(portunit_1_porta_out),
    .PORTRWWE(extraregistercontroller_1_er6_we_oe[0]), .PORTEWE(extraregistercontroller_1_er7_we_oe[0]),
    .Clock(clock_1_out), .Reset(Reset_out));  // open: PortB_In, PortC_In, PortD_In, PortB_Out, PortC_Out, PortD_Out
  or or_2 (or_2_out, and_3_out[0], and_3_out[1], and_3_out[2], and_3_out[3], and_3_out[4]);
  Hex_Digit_Display hex_digit_display_1 (.value(portunit_1_porta_out[15:12]));  // open: dp
  Hex_Digit_Display hex_digit_display_2 (.value(portunit_1_porta_out[11:8]));  // open: dp
  Hex_Digit_Display hex_digit_display_3 (.value(portunit_1_porta_out[7:4]));  // open: dp
  Hex_Digit_Display hex_digit_display_4 (.value(portunit_1_porta_out[3:0]));  // open: dp

  // Notes on the sheet:
  //   PCWE/OE
  //   MEMWE/OE
  //   HLT
  //   1WE/OE
  //   2WE/OE
  //   ALUOE
  //   Pulling Control Signal
  //   ALUSTORE
  //   WE/OE
  //   1E
  //   2E
  //   1A/D
  //   2A/D
  //   Only Div : DataIn
  //   11
  //   WE/OE
  //   ERCWE / ERCOE
  //   WE/OE
  //   Jump is special; it should always make CNR activated if JMP is 1
  //   CNR(Condition Right)
  //   1, if flag register and given condition is identical
  //   0, if not identical
endmodule

module RegisterUnit (
  input  RE_1,
  input  RE_2,
  input  OE_WE_1,
  input  OE_WE_2,
  input  [15:0] Data_Bus,
  input  Reset,
  input  ADDR_DATA_1,
  input  ADDR_DATA_2,
  input  [2:0] ControlSignal_1,
  input  [2:0] ControlSignal_2,
  input  Clock,
  output [15:0] DataBus_Out,
  output [15:0] AddressBus_Out
);

  wire and_1_out, and_2_out, and_3_out, and_4_out, and_5_out, and_6_out, and_7_out, and_8_out, and_9_out,
       and_10_out, and_11_out, and_12_out, and_13_out, and_14_out, and_15_out, and_16_out, and_17_out,
       and_18_out, decoder_1_out0, decoder_1_out1, decoder_1_out2, decoder_1_out3, decoder_1_out4,
       decoder_1_out5, decoder_1_out6, decoder_1_out7, decoder_2_out0, decoder_2_out1, decoder_2_out2,
       decoder_2_out3, decoder_2_out4, decoder_2_out5, decoder_2_out6, decoder_2_out7, not_1_out, not_2_out,
       or_1_out, or_2_out, or_3_out, or_4_out, or_5_out, or_6_out, or_7_out, or_8_out;
  wire [15:0] multiplexer_1_out, multiplexer_2_out, register_1_q, register_2_q, register_3_q, register_4_q,
       register_5_q, register_6_q, register_7_q, register_8_q;

  Decoder #(.select(3)) decoder_1 (
    .out0(decoder_1_out0), .out1(decoder_1_out1), .out2(decoder_1_out2), .out3(decoder_1_out3),
    .out4(decoder_1_out4), .out5(decoder_1_out5), .out6(decoder_1_out6), .out7(decoder_1_out7),
    .sel(ControlSignal_1));  // open: en
  Decoder #(.select(3)) decoder_2 (
    .out0(decoder_2_out0), .out1(decoder_2_out1), .out2(decoder_2_out2), .out3(decoder_2_out3),
    .out4(decoder_2_out4), .out5(decoder_2_out5), .out6(decoder_2_out6), .out7(decoder_2_out7),
    .sel(ControlSignal_2));  // open: en
  and and_1 (and_1_out, RE_1, OE_WE_1, decoder_1_out0);
  and and_2 (and_2_out, RE_2, OE_WE_2, decoder_2_out0);
  and and_3 (and_3_out, RE_1, OE_WE_1, decoder_1_out1);
  and and_4 (and_4_out, RE_2, OE_WE_2, decoder_2_out1);
  and and_5 (and_5_out, RE_1, OE_WE_1, decoder_1_out2);
  and and_6 (and_6_out, RE_2, OE_WE_2, decoder_2_out2);
  and and_7 (and_7_out, RE_1, OE_WE_1, decoder_1_out3);
  and and_8 (and_8_out, RE_2, OE_WE_2, decoder_2_out3);
  and and_9 (and_9_out, RE_1, OE_WE_1, decoder_1_out4);
  and and_10 (and_10_out, RE_2, OE_WE_2, decoder_2_out4);
  and and_11 (and_11_out, RE_1, OE_WE_1, decoder_1_out5);
  and and_12 (and_12_out, RE_2, OE_WE_2, decoder_2_out5);
  and and_13 (and_13_out, RE_1, OE_WE_1, decoder_1_out6);
  and and_14 (and_14_out, RE_2, OE_WE_2, decoder_2_out6);
  and and_15 (and_15_out, RE_1, OE_WE_1, decoder_1_out7);
  and and_16 (and_16_out, RE_2, OE_WE_2, decoder_2_out7);
  and and_17 (and_17_out, ~OE_WE_1, RE_1);  // AND_Gate
  and and_18 (and_18_out, ~OE_WE_2, RE_2);  // AND_Gate
  or or_1 (or_1_out, and_1_out, and_2_out);
  or or_2 (or_2_out, and_3_out, and_4_out);
  or or_3 (or_3_out, and_5_out, and_6_out);
  or or_4 (or_4_out, and_7_out, and_8_out);
  or or_5 (or_5_out, and_9_out, and_10_out);
  or or_6 (or_6_out, and_11_out, and_12_out);
  or or_7 (or_7_out, and_13_out, and_14_out);
  or or_8 (or_8_out, and_15_out, and_16_out);
  Register #(.width(16), .trigger("falling"), .Select("low")) register_1 (
    .D(Data_Bus), .en(or_1_out), .Q(register_1_q), .clk(Clock), .clr(Reset));
  Register #(.width(16), .trigger("falling"), .Select("low")) register_2 (
    .D(Data_Bus), .en(or_2_out), .Q(register_2_q), .clk(Clock), .clr(Reset));
  Register #(.width(16), .trigger("falling"), .Select("low")) register_3 (
    .D(Data_Bus), .en(or_3_out), .Q(register_3_q), .clk(Clock), .clr(Reset));
  Register #(.width(16), .trigger("falling"), .Select("low")) register_4 (
    .D(Data_Bus), .en(or_4_out), .Q(register_4_q), .clk(Clock), .clr(Reset));
  Register #(.width(16), .trigger("falling"), .Select("low")) register_5 (
    .D(Data_Bus), .en(or_5_out), .Q(register_5_q), .clk(Clock), .clr(Reset));
  Register #(.width(16), .trigger("falling"), .Select("low")) register_6 (
    .D(Data_Bus), .en(or_6_out), .Q(register_6_q), .clk(Clock), .clr(Reset));
  Register #(.width(16), .trigger("falling"), .Select("low")) register_7 (
    .D(Data_Bus), .en(or_7_out), .Q(register_7_q), .clk(Clock), .clr(Reset));
  Register #(.width(16), .trigger("falling"), .Select("low")) register_8 (
    .D(Data_Bus), .en(or_8_out), .Q(register_8_q), .clk(Clock), .clr(Reset));
  Multiplexer #(.select(3), .width(16)) multiplexer_1 (
    .in0(register_1_q), .in1(register_2_q), .in2(register_3_q), .in3(register_4_q), .in4(register_5_q),
    .in5(register_6_q), .in6(register_7_q), .in7(register_8_q), .out(multiplexer_1_out),
    .sel(ControlSignal_1), .en(and_17_out));
  Multiplexer #(.select(3), .width(16)) multiplexer_2 (
    .in0(register_1_q), .in1(register_2_q), .in2(register_3_q), .in3(register_4_q), .in4(register_5_q),
    .in5(register_6_q), .in6(register_7_q), .in7(register_8_q), .out(multiplexer_2_out),
    .sel(ControlSignal_2), .en(and_18_out));
  assign DataBus_Out = ADDR_DATA_1 ? multiplexer_1_out : 16'bz;  // Controlled_Buffer controlled_buffer_1
  assign AddressBus_Out = not_1_out ? multiplexer_1_out : 16'bz;  // Controlled_Buffer controlled_buffer_2
  not not_1 (not_1_out, ADDR_DATA_1);
  assign DataBus_Out = ADDR_DATA_2 ? multiplexer_2_out : 16'bz;  // Controlled_Buffer controlled_buffer_3
  assign AddressBus_Out = not_2_out ? multiplexer_2_out : 16'bz;  // Controlled_Buffer controlled_buffer_4
  not not_2 (not_2_out, ADDR_DATA_2);

  // Other names for the same wires on the sheet: Control_Signal_1[2:0] = ControlSignal_1;
  //   Control_Signal_2[2:0] = ControlSignal_2
endmodule

module InstructionQueueController (
  input  Reset,
  input  Clock,
  input  [1:0] QueueSize,
  output Stop,
  output [3:0] State,
  output Prevision
);

  wire or_1_out, or_3_out;
  wire [3:0] and_1_out, and_2_out, QS;
  wire [3:3] undriven;

  D_Flip_Flop #(.Pre_Clr_Positions("LEGACY"), .enable("true"), .NewFFLayout("false")) d_ff_1 (
    .clk(Clock), .D(State[3]), .Q(Stop), .preset(or_1_out));  // open: Qn, en, reset
  D_Flip_Flop #(.Pre_Clr_Positions("LEGACY"), .enable("true"), .NewFFLayout("false")) d_ff_2 (
    .clk(Clock), .D(Stop), .Q(State[0]), .reset(or_1_out));  // open: Qn, preset, en
  or or_1 (or_1_out, Reset, or_3_out);
  D_Flip_Flop #(.Pre_Clr_Positions("LEGACY"), .enable("true"), .NewFFLayout("false")) d_ff_3 (
    .clk(Clock), .D(State[0]), .Q(State[1]), .reset(or_1_out));  // open: Qn, preset, en
  D_Flip_Flop #(.Pre_Clr_Positions("LEGACY"), .enable("true"), .NewFFLayout("false")) d_ff_4 (
    .clk(Clock), .D(State[1]), .Q(State[2]), .reset(or_1_out));  // open: Qn, preset, en
  assign and_1_out = {undriven[3], QS[3:1]} & State;  // AND_Gate and_1, 4 bits wide
  D_Flip_Flop #(.Pre_Clr_Positions("LEGACY"), .enable("true"), .NewFFLayout("false")) d_ff_5 (
    .clk(Clock), .D(State[2]), .Q(State[3]), .reset(or_1_out));  // open: Qn, preset, en
  Decoder #(.select(2)) decoder_1 (
    .out0(QS[0]), .out1(QS[1]), .out2(QS[2]), .out3(QS[3]), .sel(QueueSize));  // open: en
  or or_2 (Prevision, and_1_out[0], and_1_out[1], and_1_out[2], and_1_out[3]);
  assign and_2_out = State & QS;  // AND_Gate and_2, 4 bits wide
  or or_3 (or_3_out, and_2_out[0], and_2_out[1], and_2_out[2], and_2_out[3]);
endmodule

module RegisterController (
  input  [2:0] Reg1,
  input  [2:0] Reg2,
  input  [2:0] InstructionType,
  output [2:0] RC1,
  output [2:0] RC2
);

  wire and_1_out, and_2_out, or_1_out;

  or or_1 (or_1_out, InstructionType[0], InstructionType[1]);
  and and_1 (and_1_out, or_1_out, ~InstructionType[2]);  // AND_Gate
  and and_2 (and_2_out, ~InstructionType[0], InstructionType[1], ~InstructionType[2]);  // AND_Gate
  and and_3 (RC1[0], and_1_out, Reg1[0]);
  and and_4 (RC1[1], and_1_out, Reg1[1]);
  and and_5 (RC1[2], and_1_out, Reg1[2]);
  and and_6 (RC2[0], and_2_out, Reg2[0]);
  and and_7 (RC2[1], and_2_out, Reg2[1]);
  and and_8 (RC2[2], and_2_out, Reg2[2]);
endmodule

module ALU (
  input  [2:0] CalcOption,
  input  [15:0] PortA,
  input  [15:0] PortB,
  output [15:0] Output,
  output [4:0] FlagOut,
  output [15:0] DivRemainder
);

  wire and_3_out;
  wire [2:0] and_1_out;
  wire [15:0] adder_1_out, and_2_out, divider_1_out, divider_1_rem, multiplier_1_out, not_1_out, or_1_out,
       subtractor_1_out, xor_1_out;

  Adder #(.width(16)) adder_1 (.a(PortA), .b(PortB), .out(adder_1_out), .cout(FlagOut[3]));  // open: cin
  assign and_1_out = CalcOption & 3'b011;  // AND_Gate and_1, 3 bits wide
  Subtractor #(.width(16)) subtractor_1 (.a(PortA), .b(PortB), .out(subtractor_1_out));  // open: bin, bout
  Multiplexer #(.select(3), .width(16)) multiplexer_1 (
    .in0(adder_1_out), .in1(subtractor_1_out), .in2(multiplier_1_out), .in3(divider_1_out), .in4(and_2_out),
    .in5(or_1_out), .in6(xor_1_out), .in7(not_1_out), .out({FlagOut[2], Output[14:0]}), .sel(CalcOption));  // open: en
  Multiplier #(.width(16)) multiplier_1 (.a(PortA), .b(PortB), .out(multiplier_1_out));  // open: cin, cout
  Divider #(.width(16)) divider_1 (.a(PortA), .b(PortB), .out(divider_1_out), .rem(divider_1_rem));  // open: upper
  assign and_2_out = PortB & PortA;  // AND_Gate and_2, 16 bits wide
  assign xor_1_out = PortB ^ PortA;  // XOR_Gate xor_1, 16 bits wide
  assign or_1_out = PortB | PortA;  // OR_Gate or_1, 16 bits wide
  and and_3 (and_3_out, and_1_out[0], and_1_out[2]);
  nor nor_1 (FlagOut[0], Output[0], Output[1], Output[2], Output[3], Output[4], Output[5], Output[6], Output[7], Output[9], Output[10], Output[11], Output[12], Output[13], Output[14], FlagOut[2], Output[8]);
  assign not_1_out = ~PortA;  // NOT_Gate not_1, 16 bits wide
  assign DivRemainder = and_3_out ? divider_1_rem : 16'bz;  // Controlled_Buffer controlled_buffer_1
  not not_2 (FlagOut[1], FlagOut[2]);
  Pull_Resistor pull_resistor_1 (.node(FlagOut[4]));

  assign Output[15] = FlagOut[2];

  // Notes on the sheet:
  //   Zero
  //   Unsigned
  //   Signed
  //   Carry
  //   Overflow
endmodule

module CentralUnit (
  input  [5:0] Instruction,
  input  OE,
  output [31:0] ControlSignal_0_31
);

  wire [5:0] multiplexer_1_out;
  wire [31:0] rom_1_data;

  Multiplexer #(.width(6), .enable("false")) multiplexer_1 (
    .in0({6{1'b0}}), .in1(Instruction), .out(multiplexer_1_out), .sel(OE));
  ROM #(.addrWidth(6), .dataWidth(32), .Select("high")) rom_1 (.addr(multiplexer_1_out), .data(rom_1_data));
  Multiplexer #(.width(32), .enable("false")) multiplexer_2 (
    .in0({32{1'b0}}), .in1(rom_1_data), .out(ControlSignal_0_31), .sel(OE));

  // Notes on the sheet:
  //   Control Signal
  //   contents of rom_1 (hex, n*v repeats v):
  //   0 270 52 4051 111 4070 8230 2012 8110 8002 c001 c010 1850 5801 1000 20002 20110 24010 80110 80002
  //   84010 80002 104010 100000 100050 4*0 40050 0 400
endmodule

module MemUnit (
  input  [15:0] AddressBus,
  input  [15:0] DataOut,
  input  [15:0] DataBusIn,
  input  ADDRIN,
  input  WE,
  input  OE,
  input  Clock,
  output [15:0] Address,
  output [15:0] DataIn,
  output [15:0] DataBusOut,
  output ClockOut,
  output ld
);

  wire and_2_out, not_1_out, or_1_out;

  assign Address = or_1_out ? AddressBus : 16'bz;  // Controlled_Buffer MAR
  or or_1 (or_1_out, ADDRIN, and_2_out, and_2_out);
  and and_1 (ClockOut, not_1_out, and_2_out);
  not not_1 (not_1_out, Clock);
  assign DataBusOut = ld ? DataOut : 16'bz;  // Controlled_Buffer Out
  assign DataIn = and_2_out ? DataBusIn : 16'bz;  // Controlled_Buffer In
  and and_2 (and_2_out, WE, ~OE);  // AND_Gate
  and and_3 (ld, ~WE, OE);  // AND_Gate
endmodule

module DataTypeDecoder (
  input  [1:0] DataType,
  input  Stop,
  output IQ1A_D,
  output IQ2A_D,
  output IQ1Out,
  output IQ2Out
);

  wire and_3_out, or_1_out;

  and and_1 (IQ1A_D, DataType[1], DataType[0]);
  and and_2 (IQ2A_D, DataType[1], ~DataType[0]);  // AND_Gate
  or or_1 (or_1_out, DataType[1], DataType[0]);
  and and_3 (and_3_out, DataType[1], ~DataType[0]);  // AND_Gate
  and and_4 (IQ1Out, or_1_out, Stop);
  and and_5 (IQ2Out, and_3_out, Stop);
endmodule

module QueueSizeDecoder (
  input  [1:0] DataType,
  output [1:0] QueueSize
);

  not not_1 (QueueSize[0], DataType[0]);
  or or_1 (QueueSize[1], DataType[0], DataType[1]);
endmodule

module InstructionTypeDecoder (
  input  [2:0] Arg1,
  input  [2:0] Arg2,
  input  [3:0] InstructionType,
  output [2:0] RC1,
  output [2:0] RC2,
  output [2:0] ALU,
  output [2:0] CJ,
  output [2:0] ERC
);

  wire [4:0] rom_1_data, rom_2_data;

  assign RC1 = rom_1_data[0] ? Arg1 : 3'bz;  // Controlled_Buffer controlled_buffer_1
  assign RC2 = rom_1_data[1] ? Arg1 : 3'bz;  // Controlled_Buffer controlled_buffer_2
  assign ALU = rom_1_data[2] ? Arg1 : 3'bz;  // Controlled_Buffer controlled_buffer_3
  assign CJ = rom_1_data[3] ? Arg1 : 3'bz;  // Controlled_Buffer controlled_buffer_4
  assign ERC = rom_1_data[4] ? Arg1 : 3'bz;  // Controlled_Buffer controlled_buffer_5
  ROM #(.addrWidth(4), .dataWidth(5), .Select("low")) rom_1 (.addr(InstructionType), .data(rom_1_data));
  assign RC1 = rom_2_data[0] ? Arg2 : 3'bz;  // Controlled_Buffer controlled_buffer_6
  assign RC2 = rom_2_data[1] ? Arg2 : 3'bz;  // Controlled_Buffer controlled_buffer_7
  assign ALU = rom_2_data[2] ? Arg2 : 3'bz;  // Controlled_Buffer controlled_buffer_8
  assign CJ = rom_2_data[3] ? Arg2 : 3'bz;  // Controlled_Buffer controlled_buffer_9
  assign ERC = rom_2_data[4] ? Arg2 : 3'bz;  // Controlled_Buffer controlled_buffer_10
  ROM #(.addrWidth(4), .dataWidth(5), .Select("low")) rom_2 (.addr(InstructionType), .data(rom_2_data));

  // Notes on the sheet:
  //   contents of rom_1 (hex, n*v repeats v):
  //   0 5*1 10 8 4
  //   contents of rom_2 (hex, n*v repeats v):
  //   0 0 2 4 8 10
endmodule

module ExtraRegisterController (
  input  WE,
  input  OE,
  input  [2:0] ERC,
  output [1:0] ER0_WE_OE,
  output [1:0] ER1_WE_OE,
  output [1:0] ER2_WE_OE,
  output [1:0] ER3_WE_OE,
  output [1:0] ER4_WE_OE,
  output [1:0] ER5_WE_OE,
  output [1:0] ER6_WE_OE,
  output [1:0] ER7_WE_OE
);

  wire decoder_1_out0, decoder_1_out1, decoder_1_out2, decoder_1_out3, decoder_1_out4, decoder_1_out5,
       decoder_1_out6, decoder_1_out7;
  wire [1:0] and_2_out, and_4_out, and_6_out, and_8_out, and_10_out, and_12_out, and_14_out, and_16_out,
       rom_1_data;

  Decoder #(.select(3), .enable("false")) decoder_1 (
    .out0(decoder_1_out0), .out1(decoder_1_out1), .out2(decoder_1_out2), .out3(decoder_1_out3),
    .out4(decoder_1_out4), .out5(decoder_1_out5), .out6(decoder_1_out6), .out7(decoder_1_out7), .sel(ERC));
  ROM #(.addrWidth(3), .dataWidth(2), .Select("low")) rom_1 (.addr(ERC), .data(rom_1_data));
  and and_1 (and_2_out[1], OE, decoder_1_out0);
  and and_2 (and_2_out[0], WE, decoder_1_out0);
  and and_3 (and_4_out[1], OE, decoder_1_out1);
  and and_4 (and_4_out[0], WE, decoder_1_out1);
  and and_5 (and_6_out[1], OE, decoder_1_out2);
  and and_6 (and_6_out[0], WE, decoder_1_out2);
  and and_7 (and_8_out[1], OE, decoder_1_out3);
  and and_8 (and_8_out[0], WE, decoder_1_out3);
  and and_9 (and_10_out[1], OE, decoder_1_out4);
  and and_10 (and_10_out[0], WE, decoder_1_out4);
  and and_11 (and_12_out[1], OE, decoder_1_out5);
  and and_12 (and_12_out[0], WE, decoder_1_out5);
  and and_13 (and_14_out[1], OE, decoder_1_out6);
  and and_14 (and_14_out[0], WE, decoder_1_out6);
  and and_15 (and_16_out[1], OE, decoder_1_out7);
  and and_16 (and_16_out[0], WE, decoder_1_out7);
  assign ER0_WE_OE = and_2_out & rom_1_data;  // AND_Gate and_17, 2 bits wide
  assign ER1_WE_OE = and_4_out & rom_1_data;  // AND_Gate and_18, 2 bits wide
  assign ER2_WE_OE = and_6_out & rom_1_data;  // AND_Gate and_19, 2 bits wide
  assign ER3_WE_OE = and_8_out & rom_1_data;  // AND_Gate and_20, 2 bits wide
  assign ER4_WE_OE = and_10_out & rom_1_data;  // AND_Gate and_21, 2 bits wide
  assign ER5_WE_OE = and_12_out & rom_1_data;  // AND_Gate and_22, 2 bits wide
  assign ER6_WE_OE = and_14_out & rom_1_data;  // AND_Gate and_23, 2 bits wide
  assign ER7_WE_OE = and_16_out & rom_1_data;  // AND_Gate and_24, 2 bits wide

  // Notes on the sheet:
  //   contents of rom_1 (hex, n*v repeats v):
  //   1 1 3 3 2 1 1 1
endmodule

module TypeDecoderUnit (
  input  [5:0] Instruction,
  output [3:0] out_2,
  output [1:0] out_3
);

  ROM #(.addrWidth(6), .dataWidth(4), .Select("low")) rom_1 (.addr(Instruction), .data(out_2));
  ROM #(.addrWidth(6), .dataWidth(2), .Select("low")) rom_2 (.addr(Instruction), .data(out_3));

  // Notes on the sheet:
  //   Instruction Type
  //   contents of rom_1 (hex, n*v repeats v):
  //   0 2 1 1 1 2 2 1 5 6 7 6 3 3 8 7 4 4 5 6 5 6 5 6 5 4*0 1
  //   Data Type
  //   Instruction Type
  //   contents of rom_2 (hex, n*v repeats v):
  //   0 0 3 1 1 0 0 3 0 3 1 0 0 1 0 3 0 0 0 3 0 1 0 1
  //   Data Type
endmodule

module PortUnit (
  input  [15:0] PortA_In,
  input  PORTWE,
  input  PORTOE,
  input  [15:0] PortB_In,
  input  [15:0] DataBusIn,
  input  [15:0] PortC_In,
  input  PORTADDRWE,
  input  [15:0] PortD_In,
  input  PORTRWWE,
  input  PORTEWE,
  input  Clock,
  input  Reset,
  output [15:0] DataBusOut,
  output [15:0] PortA_Out,
  output [15:0] PortB_Out,
  output [15:0] PortC_Out,
  output [15:0] PortD_Out
);

  wire and_1_out, and_2_out, demultiplexer_1_out0, demultiplexer_1_out1, demultiplexer_1_out2,
       demultiplexer_1_out3, multiplexer_1_out;
  wire [15:0] multiplexer_2_out, register_1_q, register_2_q, register_3_q, register_4_q, register_5_q,
       register_6_q, register_7_q;

  Register #(.width(16), .trigger("falling"), .Select("low")) register_1 (
    .D(DataBusIn), .en(PORTADDRWE), .Q(register_1_q), .clk(Clock), .clr(Reset));
  Register #(.width(16), .trigger("falling"), .Select("low")) register_2 (
    .D(DataBusIn), .en(PORTRWWE), .Q(register_2_q), .clk(Clock), .clr(Reset));
  Register #(.width(16), .trigger("falling"), .Select("low")) register_3 (
    .D(DataBusIn), .en(PORTEWE), .Q(register_3_q), .clk(Clock), .clr(Reset));
  Multiplexer #(.select(2), .enable("false")) multiplexer_1 (
    .in0(register_2_q[0]), .in1(register_2_q[1]), .in2(register_2_q[2]), .in3(register_2_q[3]),
    .out(multiplexer_1_out), .sel(register_1_q[1:0]));
  and and_1 (and_1_out, PORTOE, ~multiplexer_1_out);  // AND_Gate
  assign DataBusOut = and_1_out ? multiplexer_2_out : 16'bz;  // Controlled_Buffer controlled_buffer_1
  and and_2 (and_2_out, PORTWE, multiplexer_1_out);
  Demultiplexer #(.select(2), .enable("false")) demultiplexer_1 (
    .out0(demultiplexer_1_out0), .out1(demultiplexer_1_out1), .out2(demultiplexer_1_out2),
    .out3(demultiplexer_1_out3), .in(and_2_out), .sel(register_1_q[1:0]));
  Multiplexer #(.select(2), .width(16), .enable("false")) multiplexer_2 (
    .in0(PortA_In), .in1(PortB_In), .in2(PortC_In), .in3(PortD_In), .out(multiplexer_2_out),
    .sel(register_1_q[1:0]));
  Register #(.width(16), .trigger("falling"), .Select("low")) register_4 (
    .D(DataBusIn), .en(demultiplexer_1_out0), .Q(register_4_q), .clk(Clock), .clr(Reset));
  Register #(.width(16), .trigger("falling"), .Select("low")) register_5 (
    .D(DataBusIn), .en(demultiplexer_1_out1), .Q(register_5_q), .clk(Clock), .clr(Reset));
  Register #(.width(16), .trigger("falling"), .Select("low")) register_6 (
    .D(DataBusIn), .en(demultiplexer_1_out2), .Q(register_6_q), .clk(Clock), .clr(Reset));
  Register #(.width(16), .trigger("falling"), .Select("low")) register_7 (
    .D(DataBusIn), .en(demultiplexer_1_out3), .Q(register_7_q), .clk(Clock), .clr(Reset));
  assign PortA_Out = register_3_q[0] ? register_4_q : 16'bz;  // Controlled_Buffer controlled_buffer_2
  assign PortB_Out = register_3_q[1] ? register_5_q : 16'bz;  // Controlled_Buffer controlled_buffer_3
  assign PortC_Out = register_3_q[2] ? register_6_q : 16'bz;  // Controlled_Buffer controlled_buffer_4
  assign PortD_Out = register_3_q[3] ? register_7_q : 16'bz;  // Controlled_Buffer controlled_buffer_5
endmodule
